# Fritzing sketch IoT_Project (saved by Fritzing 0.9.10b)
breadboards: 2

parts:
  Parça1 = Arduino Uno (Rev3)
  Mod1 = Amica NodeMCU DEVKIT 1.0
  RHT1 = Humidity and Temperature Sensor RHT03
  U1 = RELAY [package=relay-jzc]
  VCC1 = Battery block 9V
  Parça2 = Soil Moisture Sensor
  M1 = gear-motor
  U2 = RELAY [package=relay-jzc]
  U3 = RELAY [package=relay-jzc]
  LED1 = smd LED [color="Red (633nm)" package="0805 [SMD]"]

nets:
  N1: Parça1.A0, Parça2.SIG
  N2: Parça1.D8, U1.NC
  GND: Parça1.GND, Mod1.pin2, Mod1.pin_9, Mod1.pin_29, RHT1.GND_2, U1.NO, Parça2.GND, U2.NO, U3.NO
  N3: Parça1.D4, RHT1.Vcc
  N4: Parça1.D5_PWM, Mod1.pin8
  N5: Parça1.D6_PWM, Mod1.pin7
  5V: Parça1.5V, RHT1.Data-signal, U1.COIL2, Parça2.VCC, U2.COIL2, U3.COIL2
  N6: U1.MAIN, M1.pin_2
  N7: U1.COIL1, VCC1.-, U2.COIL1, U3.COIL1
  N8: VCC1.+, M1.pin_1, LED1.cathode
  N9: U3.MAIN, LED1.anode

notes:
  Fan Modulu
